// Logisim project FinalProject1.circ as structural Verilog: 7 circuits, main circuit main
module main (
);

  wire AG, AR, AY, BG, BR, BY, CLK, nextstate_1_n0, nextstate_1_n1, nextstate_1_n2, PedestrianA_out,
       PedestrianB_out, Q0, Q1, Q2, request_1_req, timer_1_step;
  wire [3:0] ONES, t, TENS;

  Clock clock_1 (.out(CLK));
  LED led_1 (.in(AG));
  LED led_2 (.in(AY));
  LED led_3 (.in(AR));
  Hex_Digit_Display hex_digit_display_1 (.value(TENS));  // open: dp
  Button PedestrianA (.out(PedestrianA_out));
  Button PedestrianB (.out(PedestrianB_out));
  LED led_4 (.in(BG));
  LED led_5 (.in(BY));
  LED led_6 (.in(BR));
  Hex_Digit_Display hex_digit_display_2 (.value(ONES));  // open: dp
  Request request_1 (.PedA(PedestrianA_out), .PedB(PedestrianB_out), .W(Q2), .CLK(CLK), .REQ(request_1_req));
  NextState nextstate_1 (
    .Q2(Q2), .Q1(Q1), .Q0(Q0), .R(request_1_req), .N2(nextstate_1_n2), .N1(nextstate_1_n1),
    .N0(nextstate_1_n0));
  Timer timer_1 (.CLK(CLK), .Q2(Q2), .Q1(Q1), .t(t), .STEP(timer_1_step));
  DispLogic displogic_1 (.Q2(Q2), .t(t), .TENS(TENS), .ONES(ONES));
  StateReg statereg_1 (
    .CLK(CLK), .N2(nextstate_1_n2), .N1(nextstate_1_n1), .N0(nextstate_1_n0), .STEP(timer_1_step), .Q2(Q2),
    .Q1(Q1), .Q0(Q0));
  OutLogic outlogic_1 (.Q2(Q2), .Q1(Q1), .Q0(Q0), .AR(AR), .AY(AY), .AG(AG), .BR(BR), .BY(BY), .BG(BG));
endmodule

module Request (
  input  PedA,
  input  PedB,
  input  W,
  input  CLK,
  output REQ
);

  wire and_1_out, not_1_out, or_1_out;

  or or_1 (or_1_out, PedA, PedB);
  not not_1 (not_1_out, W);
  and and_1 (and_1_out, or_1_out, not_1_out);
  D_Flip_Flop d_ff_1 (.D(REQ), .clk(CLK), .Q(REQ), .preset(and_1_out), .reset(W));  // open: Qn
endmodule

module NextState (
  input  Q2,
  input  Q1,
  input  Q0,
  input  R,
  output N2,
  output N1,
  output N0
);

  wire and_1_out, and_2_out, and_3_out, nor_1_out, not_1_out, not_2_out, not_3_out, not_4_out, not_5_out,
       not_6_out, xor_1_out;

  not not_1 (not_1_out, Q2);
  not not_2 (not_2_out, Q1);
  not not_3 (not_3_out, R);
  not not_4 (not_4_out, Q0);
  xor xor_1 (xor_1_out, Q2, Q1);
  and and_1 (and_1_out, not_1_out, not_2_out, Q0, not_3_out);
  not not_5 (not_5_out, Q2);
  and and_2 (and_2_out, not_5_out, Q1, R);
  not not_6 (not_6_out, Q2);
  and and_3 (and_3_out, not_4_out, xor_1_out);
  nor nor_1 (nor_1_out, Q2, Q0);
  and and_4 (N2, not_6_out, Q0, R);
  or or_1 (N1, and_3_out, and_1_out);
  or or_2 (N0, nor_1_out, and_2_out);
endmodule

module StateReg (
  input  CLK,
  input  N2,
  input  N1,
  input  N0,
  input  STEP,
  output Q2,
  output Q1,
  output Q0
);

  wire D0, D1, D2;

  D_Flip_Flop d_ff_1 (.D(D2), .clk(CLK), .Q(Q2));  // open: Qn, preset, reset
  Multiplexer multiplexer_1 (.in0(Q2), .in1(N2), .out(D2), .sel(STEP));
  Multiplexer multiplexer_2 (.in0(Q1), .in1(N1), .out(D1), .sel(STEP));
  D_Flip_Flop d_ff_2 (.D(D1), .clk(CLK), .Q(Q1));  // open: Qn, preset, reset
  Multiplexer multiplexer_3 (.in0(Q0), .in1(N0), .out(D0), .sel(STEP));
  D_Flip_Flop d_ff_3 (.D(D0), .clk(CLK), .Q(Q0));  // open: Qn, preset, reset
endmodule

module OutLogic (
  input  Q2,
  input  Q1,
  input  Q0,
  output AR,
  output AY,
  output AG,
  output BR,
  output BY,
  output BG
);

  wire not_1_out, not_2_out, not_3_out, not_4_out, not_5_out, not_6_out;

  not not_1 (not_1_out, Q2);
  not not_2 (not_2_out, Q1);
  not not_3 (not_3_out, Q2);
  not not_4 (not_4_out, Q2);
  not not_5 (not_5_out, Q0);
  or or_1 (AR, Q2, Q1);
  not not_6 (not_6_out, Q1);
  and and_1 (AY, not_1_out, not_6_out, Q0);
  nor nor_1 (AG, Q2, Q1, Q0);
  or or_2 (BR, not_2_out, Q2);
  and and_2 (BY, not_3_out, Q1, Q0);
  and and_3 (BG, not_4_out, Q1, not_5_out);
endmodule

module Timer (
  input  CLK,
  input  Q2,
  input  Q1,
  output [3:0] t,
  output STEP
);

  wire and_1_out, comparator_1_eq, comparator_2_eq, multiplexer_2_out;
  wire [3:0] adder_1_out, multiplexer_1_out;

  Multiplexer #(.width(4)) multiplexer_1 (.in0(adder_1_out), .in1(4'b0000), .out(multiplexer_1_out), .sel(STEP));
  Register #(.width(4)) register_1 (.D(multiplexer_1_out), .en(1'b1), .clk(CLK), .Q(t));  // open: clr
  and and_1 (and_1_out, Q2, Q1);
  Adder #(.width(4)) adder_1 (.a(4'b0001), .b(t), .out(adder_1_out));  // open: cin, cout
  Comparator #(.width(4)) comparator_1 (.a(t), .b(4'b0010), .eq(comparator_1_eq));  // open: gt, lt
  Comparator #(.width(4)) comparator_2 (.a(t), .b(4'b1001), .eq(comparator_2_eq));  // open: gt, lt
  Multiplexer multiplexer_2 (.in0(comparator_1_eq), .in1(comparator_2_eq), .out(multiplexer_2_out), .sel(Q2));
  or or_1 (STEP, multiplexer_2_out, and_1_out);
endmodule

module DispLogic (
  input  Q2,
  input  [3:0] t,
  output [3:0] TENS,
  output [3:0] ONES
);

  wire MBS;
  wire [3:0] multiplexer_1_out, subtractor_1_out;

  Multiplexer #(.width(4)) multiplexer_1 (.in0(4'b0011), .in1(4'b1010), .out(multiplexer_1_out), .sel(Q2));
  Subtractor #(.width(4)) subtractor_1 (.a(multiplexer_1_out), .b(t), .out(subtractor_1_out));  // open: bin, bout
  Comparator #(.width(4)) comparator_1 (.a(subtractor_1_out), .b(4'b1010), .eq(MBS));  // open: gt, lt
  Multiplexer #(.width(4)) multiplexer_2 (.in0(subtractor_1_out), .in1(4'b0000), .out(ONES), .sel(MBS));
  assign TENS = {{3{1'b0}}, MBS};  // Bit_Extender bit_extender_1
endmodule
